// Logisim project PipeLine.circ as structural Verilog: 13 circuits, main circuit main
module main (
);

  wire ALU_zero, and_1_out, clock_1_out, ControlUnit_alusrc, ControlUnit_branch, ControlUnit_memread,
       ControlUnit_memtoreg, ControlUnit_memwr, ControlUnit_regdst, ControlUnit_regwr, EXMEM_branch1,
       EXMEM_equal1, EXMEM_memread1, EXMEM_memtoreg1, EXMEM_memwrite1, EXMEM_regdest1, IDEX_alusrc1,
       IDEX_branch1, IDEX_memread1, IDEX_memtoreg1, IDEX_memwrite1, IDEX_regdst1, IDEX_writereg1,
       MEMWB_out_7, MEMWB_out_8;
  wire [1:0] ControlUnit_aluopt, IDEX_aluop1;
  wire [3:0] ALUControlUnit_out_3;
  wire [4:0] EXMEM_regaddr1, IDEX_rdaddr1, IDEX_rtaddr1, multiplexer_1_out;
  wire [5:0] IDEX_funccode1;
  wire [31:0] adder_1_out, adder_2_out, ALU_out_5, DataMemory_out_6, EXMEM_alures1, EXMEM_branchaddr1,
       EXMEM_rtvalue2, IDEX_immvalue1, IDEX_pc1, IDEX_rsvalue1, IDEX_rtvalue1, IFID_instruction1, IFID_pc1,
       MEMWB_out_9, MEMWB_out_10, multiplexer_2_out, multiplexer_3_out, multiplexer_4_out, PC_q,
       RegisterFile3_readdata1, RegisterFile3_readdata2, ShiftLeft2_out_2, SignExtend_out_2, TextMem_out_2;

  Clock clock_1 (.out(clock_1_out));
  Register #(.width(32)) PC (.D(multiplexer_3_out), .en(1'b1), .clk(clock_1_out), .Q(PC_q));  // open: clr
  Adder #(.width(32)) adder_1 (.b(32'h4), .out(adder_1_out));  // open: a, cin, cout
  TextMemory TextMem (.TextAddress(PC_q), .out_2(TextMem_out_2));
  IFID1 IFID (.PC(adder_1_out), .Instruction(TextMem_out_2), .PC1(IFID_pc1), .Instruction1(IFID_instruction1));
  ControlUnit1 ControlUnit (
    .in_1(IFID_instruction1[31:26]), .Branch(ControlUnit_branch), .MemToReg(ControlUnit_memtoreg),
    .MemWr(ControlUnit_memwr), .MemRead(ControlUnit_memread), .ALUSrc(ControlUnit_alusrc),
    .ALUOpt(ControlUnit_aluopt), .RegWr(ControlUnit_regwr), .RegDst(ControlUnit_regdst));
  RegisterFile1 RegisterFile3 (
    .ReadReg1(IFID_instruction1[25:21]), .ReadReg2(IFID_instruction1[20:16]), .WriteData(multiplexer_4_out),
    .Clock(clock_1_out), .WrtieEnable(MEMWB_out_7), .ReadData1(RegisterFile3_readdata1),
    .ReadData2(RegisterFile3_readdata2));  // open: WriteReg
  SignExtend1 SignExtend (.in_1(IFID_instruction1[15:0]), .out_2(SignExtend_out_2));
  IDEX1 IDEX (
    .RegDst(ControlUnit_regdst), .MemToReg(ControlUnit_memtoreg), .Branch(ControlUnit_branch),
    .MemWrite(ControlUnit_memwr), .MemRead(ControlUnit_memread), .ALUSrc(ControlUnit_alusrc),
    .ALUOp(ControlUnit_aluopt), .WriteReg(ControlUnit_regwr), .PC(IFID_pc1),
    .RsValue(RegisterFile3_readdata1), .RtValue(RegisterFile3_readdata2), .ImmValue(SignExtend_out_2),
    .FuncCode(IFID_instruction1[5:0]), .RtAddr(IFID_instruction1[20:16]), .RdAddr(IFID_instruction1[15:11]),
    .Clock(clock_1_out), .RegDst1(IDEX_regdst1), .MemToReg1(IDEX_memtoreg1), .Branch1(IDEX_branch1),
    .MemWrite1(IDEX_memwrite1), .MemRead1(IDEX_memread1), .ALUSrc1(IDEX_alusrc1), .ALUOp1(IDEX_aluop1),
    .WriteReg1(IDEX_writereg1), .PC1(IDEX_pc1), .RsValue1(IDEX_rsvalue1), .RtValue1(IDEX_rtvalue1),
    .ImmValue1(IDEX_immvalue1), .FuncCode1(IDEX_funccode1), .RtAddr1(IDEX_rtaddr1), .RdAddr1(IDEX_rdaddr1));
  Multiplexer #(.width(5)) multiplexer_1 (
    .in0(IDEX_rtaddr1), .in1(IDEX_rdaddr1), .out(multiplexer_1_out), .sel(IDEX_writereg1));
  ShiftLeft ShiftLeft2 (.in_1(IDEX_rtvalue1), .out_2(ShiftLeft2_out_2));
  Multiplexer #(.width(32)) multiplexer_2 (
    .in0(IDEX_rtvalue1), .in1(IDEX_immvalue1), .out(multiplexer_2_out), .sel(IDEX_alusrc1));
  ALUControlUnit1 ALUControlUnit (._0000___ADD(IDEX_funccode1), .ALUOpt(IDEX_aluop1), .out_3(ALUControlUnit_out_3));
  Adder #(.width(32)) adder_2 (.a(IDEX_pc1), .b(ShiftLeft2_out_2), .out(adder_2_out));  // open: cin, cout
  ALU1 ALU (
    .Input1(IDEX_rsvalue1), .Input2(multiplexer_2_out), .ALUOpt(ALUControlUnit_out_3), .Zero(ALU_zero),
    .out_5(ALU_out_5));
  EXMEM1 EXMEM (
    .RegDest(IDEX_regdst1), .MemToReg(IDEX_memtoreg1), .Branch(IDEX_branch1), .MemWrite(IDEX_memwrite1),
    .MemRead(IDEX_memread1), .BranchAddr(adder_2_out), .Equal(ALU_zero), .ALURes(ALU_out_5),
    .RtValue1(IDEX_rtvalue1), .RegAddr(multiplexer_1_out), .Clock(clock_1_out), .RegDest1(EXMEM_regdest1),
    .MemToReg1(EXMEM_memtoreg1), .Branch1(EXMEM_branch1), .MemWrite1(EXMEM_memwrite1),
    .MemRead1(EXMEM_memread1), .BranchAddr1(EXMEM_branchaddr1), .Equal1(EXMEM_equal1),
    .ALURes1(EXMEM_alures1), .RtValue2(EXMEM_rtvalue2), .RegAddr1(EXMEM_regaddr1));
  Multiplexer #(.width(32)) multiplexer_3 (
    .in0(adder_1_out), .in1(EXMEM_branchaddr1), .out(multiplexer_3_out), .sel(and_1_out));
  and and_1 (and_1_out, EXMEM_branch1, EXMEM_equal1);
  DataMemory1 DataMemory (
    .Address(EXMEM_alures1), .WriteData(EXMEM_rtvalue2), .Clock(clock_1_out), .MemRead(EXMEM_memread1),
    .MemWrite(EXMEM_memwrite1), .out_6(DataMemory_out_6));
  MEMWB1 MEMWB (
    .in_1(EXMEM_regdest1), .in_2(EXMEM_memtoreg1), .in_3(DataMemory_out_6), .in_4(EXMEM_alures1),
    .in_5(EXMEM_regaddr1), .in_6(clock_1_out), .out_7(MEMWB_out_7), .out_8(MEMWB_out_8), .out_9(MEMWB_out_9),
    .out_10(MEMWB_out_10));  // open: out_11
  Multiplexer #(.width(32)) multiplexer_4 (
    .in0(MEMWB_out_9), .in1(MEMWB_out_10), .out(multiplexer_4_out), .sel(MEMWB_out_8));
endmodule

module TextMemory (
  input  [31:0] TextAddress,
  output [31:0] out_2
);

  ROM #(.addrWidth(22), .dataWidth(32)) rom_1 (.addr(TextAddress[23:2]), .data(out_2));

  // Notes on the sheet:
  //   contents of rom_1 (hex, n*v repeats v):
  //   14b4820 10000064 0 0 10000064
endmodule

module RegisterFile1 (
  input  WrtieEnable,
  input  [4:0] ReadReg1,
  input  [4:0] ReadReg2,
  input  [4:0] WriteReg,
  input  [31:0] WriteData,
  input  Clock,
  output [31:0] ReadData1,
  output [31:0] ReadData2
);

  wire and_1_out, and_2_out, and_3_out, and_4_out, and_5_out, and_6_out, and_7_out, and_8_out, and_9_out,
       and_10_out, and_11_out, and_12_out, and_13_out, and_14_out, and_15_out, and_16_out, and_17_out,
       and_18_out, and_19_out, and_20_out, and_21_out, and_22_out, and_23_out, and_24_out, and_25_out,
       and_26_out, and_27_out, and_28_out, and_29_out, and_30_out, and_31_out, decoder_1_out1,
       decoder_1_out2, decoder_1_out3, decoder_1_out4, decoder_1_out5, decoder_1_out6, decoder_1_out7,
       decoder_1_out8, decoder_1_out9, decoder_1_out10, decoder_1_out11, decoder_1_out12, decoder_1_out13,
       decoder_1_out14, decoder_1_out15, decoder_1_out16, decoder_1_out17, decoder_1_out18, decoder_1_out19,
       decoder_1_out20, decoder_1_out21, decoder_1_out22, decoder_1_out23, decoder_1_out24, decoder_1_out25,
       decoder_1_out26, decoder_1_out27, decoder_1_out28, decoder_1_out29, decoder_1_out30, decoder_1_out31;
  wire [31:0] r0_q, r1_q, r2_q, r3_q, r4_q, r5_q, r6_q, r7_q, r8_q, r9_q, r10_q, r11_q, r12_q, r13_q, r14_q,
       r15_q, r16_q, r17_q, r18_q, r19_q, r20_q, r21_q, r22_q, r23_q, r24_q, r25_q, r26_q, r27_q, r28_q,
       r29_q, r30_q, r31_q;

  Decoder #(.enable("false"), .select(5)) decoder_1 (
    .out1(decoder_1_out1), .out2(decoder_1_out2), .out3(decoder_1_out3), .out4(decoder_1_out4),
    .out5(decoder_1_out5), .out6(decoder_1_out6), .out7(decoder_1_out7), .out8(decoder_1_out8),
    .out9(decoder_1_out9), .out10(decoder_1_out10), .out11(decoder_1_out11), .out12(decoder_1_out12),
    .out13(decoder_1_out13), .out14(decoder_1_out14), .out15(decoder_1_out15), .out16(decoder_1_out16),
    .out17(decoder_1_out17), .out18(decoder_1_out18), .out19(decoder_1_out19), .out20(decoder_1_out20),
    .out21(decoder_1_out21), .out22(decoder_1_out22), .out23(decoder_1_out23), .out24(decoder_1_out24),
    .out25(decoder_1_out25), .out26(decoder_1_out26), .out27(decoder_1_out27), .out28(decoder_1_out28),
    .out29(decoder_1_out29), .out30(decoder_1_out30), .out31(decoder_1_out31), .sel(WriteReg));  // open: out0
  and and_1 (and_1_out, WrtieEnable, decoder_1_out1);
  and and_2 (and_2_out, WrtieEnable, decoder_1_out2);
  and and_3 (and_3_out, WrtieEnable, decoder_1_out3);
  and and_4 (and_4_out, WrtieEnable, decoder_1_out4);
  and and_5 (and_5_out, WrtieEnable, decoder_1_out5);
  and and_6 (and_6_out, WrtieEnable, decoder_1_out6);
  and and_7 (and_7_out, WrtieEnable, decoder_1_out7);
  and and_8 (and_8_out, WrtieEnable, decoder_1_out8);
  and and_9 (and_9_out, WrtieEnable, decoder_1_out9);
  and and_10 (and_10_out, WrtieEnable, decoder_1_out10);
  and and_11 (and_11_out, WrtieEnable, decoder_1_out11);
  and and_12 (and_12_out, WrtieEnable, decoder_1_out12);
  and and_13 (and_13_out, WrtieEnable, decoder_1_out13);
  and and_14 (and_14_out, WrtieEnable, decoder_1_out14);
  and and_15 (and_15_out, WrtieEnable, decoder_1_out15);
  and and_16 (and_16_out, WrtieEnable, decoder_1_out16);
  and and_17 (and_17_out, WrtieEnable, decoder_1_out17);
  and and_18 (and_18_out, WrtieEnable, decoder_1_out18);
  and and_19 (and_19_out, WrtieEnable, decoder_1_out19);
  and and_20 (and_20_out, WrtieEnable, decoder_1_out20);
  and and_21 (and_21_out, WrtieEnable, decoder_1_out21);
  and and_22 (and_22_out, WrtieEnable, decoder_1_out22);
  and and_23 (and_23_out, WrtieEnable, decoder_1_out23);
  and and_24 (and_24_out, WrtieEnable, decoder_1_out24);
  and and_25 (and_25_out, WrtieEnable, decoder_1_out25);
  and and_26 (and_26_out, WrtieEnable, decoder_1_out26);
  and and_27 (and_27_out, WrtieEnable, decoder_1_out27);
  and and_28 (and_28_out, WrtieEnable, decoder_1_out28);
  and and_29 (and_29_out, WrtieEnable, decoder_1_out29);
  and and_30 (and_30_out, WrtieEnable, decoder_1_out30);
  and and_31 (and_31_out, WrtieEnable, decoder_1_out31);
  Register #(.width(32)) r0 (.D(WriteData), .en(1'b0), .clk(Clock), .Q(r0_q));  // open: clr
  Register #(.width(32)) r1 (.D(WriteData), .en(and_1_out), .clk(Clock), .Q(r1_q));  // open: clr
  Register #(.width(32)) r2 (.D(WriteData), .en(and_2_out), .clk(Clock), .Q(r2_q));  // open: clr
  Register #(.width(32)) r3 (.D(WriteData), .en(and_3_out), .clk(Clock), .Q(r3_q));  // open: clr
  Register #(.width(32)) r4 (.D(WriteData), .en(and_4_out), .clk(Clock), .Q(r4_q));  // open: clr
  Register #(.width(32)) r5 (.D(WriteData), .en(and_5_out), .clk(Clock), .Q(r5_q));  // open: clr
  Register #(.width(32)) r6 (.D(WriteData), .en(and_6_out), .clk(Clock), .Q(r6_q));  // open: clr
  Register #(.width(32)) r7 (.D(WriteData), .en(and_7_out), .clk(Clock), .Q(r7_q));  // open: clr
  Register #(.width(32)) r8 (.D(WriteData), .en(and_8_out), .clk(Clock), .Q(r8_q));  // open: clr
  Register #(.width(32)) r9 (.D(WriteData), .en(and_9_out), .clk(Clock), .Q(r9_q));  // open: clr
  Register #(.width(32)) r10 (.D(WriteData), .en(and_10_out), .clk(Clock), .Q(r10_q));  // open: clr
  Register #(.width(32)) r11 (.D(WriteData), .en(and_11_out), .clk(Clock), .Q(r11_q));  // open: clr
  Register #(.width(32)) r12 (.D(WriteData), .en(and_12_out), .clk(Clock), .Q(r12_q));  // open: clr
  Register #(.width(32)) r13 (.D(WriteData), .en(and_13_out), .clk(Clock), .Q(r13_q));  // open: clr
  Register #(.width(32)) r14 (.D(WriteData), .en(and_14_out), .clk(Clock), .Q(r14_q));  // open: clr
  Register #(.width(32)) r15 (.D(WriteData), .en(and_15_out), .clk(Clock), .Q(r15_q));  // open: clr
  Register #(.width(32)) r16 (.D(WriteData), .en(and_16_out), .clk(Clock), .Q(r16_q));  // open: clr
  Register #(.width(32)) r17 (.D(WriteData), .en(and_17_out), .clk(Clock), .Q(r17_q));  // open: clr
  Register #(.width(32)) r18 (.D(WriteData), .en(and_18_out), .clk(Clock), .Q(r18_q));  // open: clr
  Register #(.width(32)) r19 (.D(WriteData), .en(and_19_out), .clk(Clock), .Q(r19_q));  // open: clr
  Register #(.width(32)) r20 (.D(WriteData), .en(and_20_out), .clk(Clock), .Q(r20_q));  // open: clr
  Register #(.width(32)) r21 (.D(WriteData), .en(and_21_out), .clk(Clock), .Q(r21_q));  // open: clr
  Register #(.width(32)) r22 (.D(WriteData), .en(and_22_out), .clk(Clock), .Q(r22_q));  // open: clr
  Register #(.width(32)) r23 (.D(WriteData), .en(and_23_out), .clk(Clock), .Q(r23_q));  // open: clr
  Register #(.width(32)) r24 (.D(WriteData), .en(and_24_out), .clk(Clock), .Q(r24_q));  // open: clr
  Register #(.width(32)) r25 (.D(WriteData), .en(and_25_out), .clk(Clock), .Q(r25_q));  // open: clr
  Register #(.width(32)) r26 (.D(WriteData), .en(and_26_out), .clk(Clock), .Q(r26_q));  // open: clr
  Register #(.width(32)) r27 (.D(WriteData), .en(and_27_out), .clk(Clock), .Q(r27_q));  // open: clr
  Register #(.width(32)) r28 (.D(WriteData), .en(and_28_out), .clk(Clock), .Q(r28_q));  // open: clr
  Register #(.width(32)) r29 (.D(WriteData), .en(and_29_out), .clk(Clock), .Q(r29_q));  // open: clr
  Register #(.width(32)) r30 (.D(WriteData), .en(and_30_out), .clk(Clock), .Q(r30_q));  // open: clr
  Register #(.width(32)) r31 (.D(WriteData), .en(and_31_out), .clk(Clock), .Q(r31_q));  // open: clr
  Multiplexer #(.select(5), .width(32)) multiplexer_1 (
    .in0(r0_q), .in1(r1_q), .in2(r2_q), .in3(r3_q), .in4(r4_q), .in5(r5_q), .in6(r6_q), .in7(r7_q),
    .in8(r8_q), .in9(r9_q), .in10(r10_q), .in11(r11_q), .in12(r12_q), .in13(r13_q), .in14(r14_q),
    .in15(r15_q), .in16(r16_q), .in17(r17_q), .in18(r18_q), .in19(r19_q), .in20(r20_q), .in21(r21_q),
    .in22(r22_q), .in23(r23_q), .in24(r24_q), .in25(r25_q), .in26(r26_q), .in27(r27_q), .in28(r28_q),
    .in29(r29_q), .in30(r30_q), .in31(r31_q), .out(ReadData1), .sel(ReadReg1));
  Multiplexer #(.select(5), .width(32)) multiplexer_2 (
    .in0(r0_q), .in1(r1_q), .in2(r2_q), .in3(r3_q), .in4(r4_q), .in5(r5_q), .in6(r6_q), .in7(r7_q),
    .in8(r8_q), .in9(r9_q), .in10(r10_q), .in11(r11_q), .in12(r12_q), .in13(r13_q), .in14(r14_q),
    .in15(r15_q), .in16(r16_q), .in17(r17_q), .in18(r18_q), .in19(r19_q), .in20(r20_q), .in21(r21_q),
    .in22(r22_q), .in23(r23_q), .in24(r24_q), .in25(r25_q), .in26(r26_q), .in27(r27_q), .in28(r28_q),
    .in29(r29_q), .in30(r30_q), .in31(r31_q), .out(ReadData2), .sel(ReadReg2));
endmodule

module ALU1 (
  input  [31:0] Input1,
  input  [31:0] Input2,
  input  [3:0] ALUOpt,
  output Zero,
  output [31:0] out_5
);

  wire [0:0] comparator_1_lt;
  wire [31:0] adder_1_out, and_1_out, nor_1_out, or_1_out, subtractor_1_out;

  assign and_1_out = Input1 & Input2;  // AND_Gate and_1, 32 bits wide
  assign or_1_out = Input1 | Input2;  // OR_Gate or_1, 32 bits wide
  Adder #(.width(32)) adder_1 (.a(Input1), .b(Input2), .out(adder_1_out));  // open: cin, cout
  Subtractor #(.width(32)) subtractor_1 (.a(Input1), .b(Input2), .out(subtractor_1_out));  // open: bin, bout
  Comparator #(.width(32)) comparator_1 (.a(Input1), .b(Input2), .lt(comparator_1_lt[0]));  // open: gt, eq
  assign nor_1_out = ~(Input1 | Input2);  // NOR_Gate nor_1, 32 bits wide
  Multiplexer #(.select(4), .width(32)) multiplexer_1 (
    .in0(and_1_out), .in1(or_1_out), .in2(adder_1_out), .in6(subtractor_1_out),
    .in7({{31{1'b0}}, comparator_1_lt[0]}), .in12(nor_1_out), .out(out_5), .sel(ALUOpt));  // open: in3, in4, in5, in8, in9, in10, in11, in13, in14, in15
  Comparator #(.width(32)) comparator_2 (.a({32{1'b0}}), .b(out_5), .eq(Zero));  // open: gt, lt

  // Notes on the sheet:
  //   0000    AND
  //   0001    OR 
  //   0010    ADD
  //   0110    SUB
  //   0111    SLT
  //   1100    NOR
endmodule

module SignExtend1 (
  input  [15:0] in_1,
  output [31:0] out_2
);


  assign out_2 = {{17{in_1[15]}}, in_1[14:0]};
endmodule

module ControlUnit1 (
  input  [5:0] in_1,
  output Branch,
  output MemToReg,
  output MemWr,
  output MemRead,
  output ALUSrc,
  output [1:0] ALUOpt,
  output RegWr,
  output RegDst
);

  ROM #(.addrWidth(6), .dataWidth(9)) rom_1 (
    .addr(in_1), .data({RegDst, RegWr, ALUOpt, ALUSrc, MemRead, MemWr, MemToReg, Branch}));

  // Notes on the sheet:
  //   contents of rom_1 (hex, n*v repeats v):
  //   1c2 0 0 0 21
endmodule

module ALUControlUnit1 (
  input  [1:0] ALUOpt,
  input  [5:0] _0000___ADD,
  output [3:0] out_3
);

  wire [3:0] multiplexer_1_out;

  Multiplexer #(.select(4), .width(4)) multiplexer_1 (
    .in0(4'b0010), .in2(4'b0110), .in4(4'b0000), .in5(4'b0001), .in10(4'b0111), .out(multiplexer_1_out),
    .sel(_0000___ADD[3:0]));  // open: in1, in3, in6, in7, in8, in9, in11, in12, in13, in14, in15
  Multiplexer #(.select(2), .width(4)) multiplexer_2 (
    .in0(4'b0010), .in1(4'b0110), .in2(multiplexer_1_out), .out(out_3), .sel(ALUOpt));  // open: in3

  // Notes on the sheet:
  //   Ignore first two bits
  //   0010 - SUB
  //   0100 - AND
  //   0101 - OR
  //   1010 - SLT
  //   0000 - AND
  //   0001 - OR  
  //   0010 - ADD
  //   0110 - SUB
  //   0111 - SLT
  //   1100 - NOR
  //   Note: using a selctior11 (3)
  //   is an error, and results are undefined,
endmodule

module DataMemory1 (
  input  MemRead,
  input  MemWrite,
  input  [31:0] Address,
  input  [31:0] WriteData,
  input  Clock,
  output [31:0] out_6
);

  RAM #(.addrWidth(22), .dataWidth(32)) ram_1 (
    .addr(Address[23:2]), .we(MemWrite), .oe(MemRead), .clk(Clock), .din(WriteData), .dout(out_6));
endmodule

module ShiftLeft (
  input  [31:0] in_1,
  output [31:0] out_2
);


  assign out_2 = {in_1[29:0], 2'b00};
endmodule

module IFID1 (
  input  [31:0] PC,
  input  [31:0] Instruction,
  output [31:0] PC1,
  output [31:0] Instruction1
);


  assign Instruction1 = Instruction;
  assign PC1 = PC;
endmodule

module IDEX1 (
  input  RegDst,
  input  MemToReg,
  input  Branch,
  input  MemWrite,
  input  MemRead,
  input  ALUSrc,
  input  [1:0] ALUOp,
  input  WriteReg,
  input  [31:0] PC,
  input  [31:0] RsValue,
  input  [31:0] RtValue,
  input  [31:0] ImmValue,
  input  [5:0] FuncCode,
  input  [4:0] RtAddr,
  input  [4:0] RdAddr,
  input  Clock,
  output RegDst1,
  output MemToReg1,
  output Branch1,
  output MemWrite1,
  output MemRead1,
  output ALUSrc1,
  output [1:0] ALUOp1,
  output WriteReg1,
  output [31:0] PC1,
  output [31:0] RsValue1,
  output [31:0] RtValue1,
  output [31:0] ImmValue1,
  output [5:0] FuncCode1,
  output [4:0] RtAddr1,
  output [4:0] RdAddr1
);

  Register #(.width(1)) register_1 (.D(RegDst), .en(1'b1), .clk(Clock), .Q(RegDst1));  // open: clr
  Register #(.width(1)) register_2 (.D(MemToReg), .en(1'b1), .clk(Clock), .Q(MemToReg1));  // open: clr
  Register #(.width(1)) register_3 (.D(Branch), .en(1'b1), .clk(Clock), .Q(Branch1));  // open: clr
  Register #(.width(1)) register_4 (.D(MemWrite), .en(1'b1), .clk(Clock), .Q(MemWrite1));  // open: clr
  Register #(.width(1)) register_5 (.D(MemRead), .en(1'b1), .clk(Clock), .Q(MemRead1));  // open: clr
  Register #(.width(1)) register_6 (.D(ALUSrc), .en(1'b1), .clk(Clock), .Q(ALUSrc1));  // open: clr
  Register #(.width(2)) register_7 (.D(ALUOp), .en(1'b1), .clk(Clock), .Q(ALUOp1));  // open: clr
  Register #(.width(1)) register_8 (.D(WriteReg), .en(1'b1), .clk(Clock), .Q(WriteReg1));  // open: clr
  Register #(.width(32)) register_9 (.D(PC), .en(1'b1), .clk(Clock), .Q(PC1));  // open: clr
  Register #(.width(32)) register_10 (.D(RsValue), .en(1'b1), .clk(Clock), .Q(RsValue1));  // open: clr
  Register #(.width(32)) register_11 (.D(RtValue), .en(1'b1), .clk(Clock), .Q(RtValue1));  // open: clr
  Register #(.width(32)) register_12 (.D(ImmValue), .en(1'b1), .clk(Clock), .Q(ImmValue1));  // open: clr
  Register #(.width(6)) register_13 (.D(FuncCode), .en(1'b1), .clk(Clock), .Q(FuncCode1));  // open: clr
  Register #(.width(5)) register_14 (.D(RtAddr), .en(1'b1), .clk(Clock), .Q(RtAddr1));  // open: clr
  Register #(.width(5)) register_15 (.D(RdAddr), .en(1'b1), .clk(Clock), .Q(RdAddr1));  // open: clr
endmodule

module EXMEM1 (
  input  RegDest,
  input  MemToReg,
  input  Branch,
  input  MemWrite,
  input  MemRead,
  input  [31:0] BranchAddr,
  input  Equal,
  input  [31:0] ALURes,
  input  [31:0] RtValue1,
  input  [4:0] RegAddr,
  input  Clock,
  output RegDest1,
  output MemToReg1,
  output Branch1,
  output MemWrite1,
  output MemRead1,
  output [31:0] BranchAddr1,
  output Equal1,
  output [31:0] ALURes1,
  output [31:0] RtValue2,
  output [4:0] RegAddr1
);

  Register #(.width(1)) register_1 (.D(RegDest), .en(1'b1), .clk(Clock), .Q(RegDest1));  // open: clr
  Register #(.width(1)) register_2 (.D(MemToReg), .en(1'b1), .clk(Clock), .Q(MemToReg1));  // open: clr
  Register #(.width(1)) register_3 (.D(Branch), .en(1'b1), .clk(Clock), .Q(Branch1));  // open: clr
  Register #(.width(1)) register_4 (.D(MemWrite), .en(1'b1), .clk(Clock), .Q(MemWrite1));  // open: clr
  Register #(.width(1)) register_5 (.D(MemRead), .en(1'b1), .clk(Clock), .Q(MemRead1));  // open: clr
  Register #(.width(32)) register_6 (.D(BranchAddr), .en(1'b1), .clk(Clock), .Q(BranchAddr1));  // open: clr
  Register #(.width(1)) register_7 (.D(Equal), .en(1'b1), .clk(Clock), .Q(Equal1));  // open: clr
  Register #(.width(32)) register_8 (.D(ALURes), .en(1'b1), .clk(Clock), .Q(ALURes1));  // open: clr
  Register #(.width(32)) register_9 (.D(RtValue1), .en(1'b1), .clk(Clock), .Q(RtValue2));  // open: clr
  Register #(.width(5)) register_10 (.D(RegAddr), .en(1'b1), .clk(Clock), .Q(RegAddr1));  // open: clr
endmodule

module MEMWB1 (
  input  in_1,
  input  in_2,
  input  [31:0] in_3,
  input  [31:0] in_4,
  input  [4:0] in_5,
  input  in_6,
  output out_7,
  output out_8,
  output [31:0] out_9,
  output [31:0] out_10,
  output [4:0] out_11
);

  Register #(.width(1)) register_1 (.D(in_1), .en(1'b1), .clk(in_6), .Q(out_7));  // open: clr
  Register #(.width(1)) register_2 (.D(in_2), .en(1'b1), .clk(in_6), .Q(out_8));  // open: clr
  Register #(.width(32)) register_3 (.D(in_3), .en(1'b1), .clk(in_6), .Q(out_9));  // open: clr
  Register #(.width(32)) register_4 (.D(in_4), .en(1'b1), .clk(in_6), .Q(out_10));  // open: clr
  Register #(.width(5)) register_5 (.D(in_5), .en(1'b1), .clk(in_6), .Q(out_11));  // open: clr
endmodule
